# Fritzing sketch version0 (saved by Fritzing 0.9.3b)

parts:
  S1 = H-Bridge with L298N
  WeMos_D1_Mini1 = WeMos D1 Mini
  hc-sr1 = hc-sr04  # not connected
  Part1 = QMC5883L - Triple Axis Magnetometer Breakout
  VCC1 = 4 x AAA Battery Mount
  R1 = Resistor [tolerance=±5% resistance=220 package=THT]
  R2 = Resistor [tolerance=±5% resistance=220 package=THT]

nets:
  N1: S1.12V, VCC1.+, R1.Pin_0
  GND: S1.GND, WeMos_D1_Mini1.G, Part1.GND, VCC1.-, R2.Pin_1
  5V: S1.5V, WeMos_D1_Mini1.5V, Part1.VCC
  N2: S1.ENA, WeMos_D1_Mini1.D8
  N3: S1.IN1, WeMos_D1_Mini1.D6
  N4: S1.IN2, WeMos_D1_Mini1.D5
  N5: S1.IN3, WeMos_D1_Mini1.D0
  N6: S1.IN4, WeMos_D1_Mini1.D3
  N7: S1.ENB, WeMos_D1_Mini1.D7
  N8: WeMos_D1_Mini1.A0, R2.Pin_0
  N9: WeMos_D1_Mini1.D1, Part1.SCL
  N10: WeMos_D1_Mini1.D2, Part1.SDA

notes:
  Voltage Divider 6V=>1V

custom parts:
  H-Bridge with L298N: h-bridge

// code stored in the sketch: version0.ino
#include "SerialTransfer.h"
#include <QMC5883LCompass.h>
#include <Wire.h>


// ===================================================================
// https://www.youtube.com/watch?v=bsB5shP3vls


// ------------------ Serial ------------------
//SerialTransfer myTransfer;


struct __attribute__((packed)) CONTROLLER {
  long pitch;
  long yaw;
  long roll;
  long throttle;
  long aux1;
  long aux2;
  long aux3;
  long aux4;
} commandStruct;




struct __attribute__((packed)) SENSORS {
  float sonar1;
  float sonar2;
  float sonar3;
  long heading;
  long ax;
} sensorStruct;


// ------------------ MAG ------------------
/* Assign a unique ID to this sensor at the same time */
QMC5883LCompass compass;


// ------------------ L298N ------------------
// PWM Wemos D1
#define enA D8
#define in1 D6
#define in2 D5
#define in3 D0
#define in4 A0
#define enB D7


float ur = 0.0;
float ul = 0.0;


void setup()
{
  // ------------------ Serial ------------------
  Wire.begin();


  Serial.begin(115200);
  //myTransfer.begin(Serial);
  Serial.println("Beginning");
  // ------------------ MAG ------------------



  //compass.init();
  //compass.setCalibration(-1700, 840, 0, 3056, -2957, 0);
  Serial.println("Compass initialized");
  


  // ------------------ L298N ------------------
  pinMode(enA, OUTPUT);
  pinMode(enB, OUTPUT);
  pinMode(in1, OUTPUT);
  pinMode(in2, OUTPUT);
  pinMode(in3, OUTPUT);
  pinMode(in4, OUTPUT);





  delay(3000);







// ===================================================================
void moveMotor(int dirPin1, int dirPin2, int enaPin, float u, int speedMin=70, int speedThres=10) {
  float speed = fabs(u); 

  if (speed > 255 ) {
    speed = 255;
  }


  speed = map(speed, 0, 255, 70, 255);


  if (u<0){
    digitalWrite(dirPin1, LOW);
    digitalWrite(dirPin2, HIGH);
  } else {
    digitalWrite(dirPin1, HIGH);
    digitalWrite(dirPin2, LOW);
  }
  analogWrite(enaPin, speed); // Send PWM signal to motor A
}


// ===================================================================
void loop(){


  // Record the time
  currentMillis = millis();


  // Control Motor
  moveMotor(in1, in2, enA,  ur);
  moveMotor(in3, in4, enB,  ul);



  //Compass
  //compass.read();
  //int heading = compass.getAzimuth();


  //erial.print(", ");
  //Serial.print(heading);
  // Serial.print(", ");
  // Serial.print(fabs(ur)); // 0 = N, 4 = E, 8 = S, 12 = W
  // Serial.print(", ");
  // Serial.print(fabs(ul)); // 0 = N, 4 = E, 8 = S, 12 = W


  Serial.println();


//   if(myTransfer.available())
//   {


//     // ------------------ Receive Serial ------------------
//     // use this variable to keep track of how many
//     // bytes we've processed from the receive buffer
//     uint16_t recSize = 0;
//     recSize = myTransfer.rxObj(commandStruct, recSize);
    


//     // ------------------ IMU and Compass ------------------


//     long heading;
//     // Read compass values
//     compass.read();


//     // Return Azimuth reading
//     heading = compass.getAzimuth();


//     sensorStruct.heading = float(heading);
//     sensorStruct.ax = float(motorSpeedB);
    
    


//     // ------------------ Send Serial ------------------
//     uint16_t sendSize = 0;
//     sendSize = myTransfer.txObj(sensorStruct, sendSize);
//     myTransfer.sendData(sendSize);
//   }

}



}
